# Fritzing sketch 2Wheels_3_Sensors (saved by Fritzing 0.9.3b)
breadboards: 1

parts:
  Part1 = Arduino Uno (Rev3) - ICSP
  wheels_3_4 = L293D [package=THT]
  VCC1 = 4 x AAA Battery Mount
  Wheel_4 = DC Motor [part_number="Wheel 4"]
  Wheel_3 = DC Motor [part_number="Wheel 3"]
  Left = hc-sr04
  Mid = hc-sr04
  Right = hc-sr04
  IR1_right = TSOP312.., 314.. [package=THT]
  IR2_mid = TSOP312.., 314.. [package=THT]
  IR3_left = TSOP312.., 314.. [package=THT]

nets:
  N1: Part1.A3, IR3_left.Vs
  N2: Part1.A4/SDA, IR2_mid.Vs
  N3: Part1.A5/SCL, IR1_right.Vs
  N4: Part1.ICSP_MISO, Part1.D12/MISO, wheels_3_4.In_4
  N5: Part1.ICSP_MOSI, Part1.D11_PWM/MOSI, Left.Echo
  N6: Part1.D8, wheels_3_4.In_3
  N7: Part1.D10_PWM/SS, wheels_3_4.Enable_1, wheels_3_4.Enable_2
  N8: Part1.D2, Left.Trig, Mid.Trig, Right.Trig
  N9: Part1.D3_PWM, Right.Echo
  N10: Part1.D4, wheels_3_4.In_2
  N11: Part1.D5_PWM, Mid.Echo
  N12: Part1.D7, wheels_3_4.In_1
  VCC: Part1.5V, Left.VCC, Mid.VCC, Right.VCC, IR1_right.Data, IR2_mid.Data, IR3_left.Data
  GND: Part1.GND, IR1_right.GND, IR2_mid.GND, IR3_left.GND
  N13: wheels_3_4.Out_1_(_Controlled_by_Enable_1_), Wheel_3.pin_1
  GND_2: wheels_3_4.0V, VCC1.-, Left.GND, Mid.GND, Right.GND
  N14: wheels_3_4.Out_2_(_Controlled_by_Enable_1_), Wheel_3.pin_2
  N15: wheels_3_4.+Vmotor, wheels_3_4.+V, VCC1.+
  N16: wheels_3_4.Out_3_(_Controlled_by_Enable_2_), Wheel_4.pin_2
  N17: wheels_3_4.Out_4_(_Controlled_by_Enable_2_), Wheel_4.pin_1
